# Fritzing sketch wiring-withANano (saved by Fritzing 0.9.6b)
breadboards: 4

parts:
  A1 = Waveshare ESP32-Pico  # not connected
  M1 = RPlidar A2M8 [package=THT]  # not connected
  DC_Mot_Enc1 = DC Motor with two-phase hall-encoder [part_number=VT-E-G25A-06-177E]  # not connected
  Part1 = Arduino Nano (Rev3.0)
  DC_Mot_Enc2 = DC Motor with two-phase hall-encoder [part_number=VT-E-G25A-06-177E]  # not connected
  DC_Mot_Enc3 = DC Motor with two-phase hall-encoder [part_number=VT-E-G25A-06-177E]  # not connected
  DC_Mot_Enc4 = DC Motor with two-phase hall-encoder [part_number=VT-E-G25A-06-177E]  # not connected
  HC-SR04_Sensor_1 = HC-SR04 Ultrasonic Distance Sensor
  U1 = LIPO-1000mAh [package=lipo-1000]
  M2 = RioRand LM2596
  X1 = USB Connectors [package=usb-microb]  # not connected
  M3 = fc-51 [package=THT]
  M4 = fc-51 [package=THT]
  A3 = Sparkfun sen18642  # not connected
  Part3 = InvenSense MPU6050
  A4 = Hi-link HLK-LD2410C  # not connected
  A5 = Jetson Nano  # not connected
  U2 = LIPO-2000mAh [package=lipo-2000]  # not connected
  Part6 = I2C level shifter bidirectional
  U3 = LIPO-1000mAh [package=lipo-1000]
  M5 = RioRand LM2596
  X2 = USB Connectors [package=usb-microb]  # not connected
  M6 = fc-51 [package=THT]
  M7 = fc-51 [package=THT]
  A6 = Sparkfun sen18642
  Part7 = InvenSense MPU6050
  A7 = Hi-link HLK-LD2410C
  U4 = LIPO-2000mAh [package=lipo-2000]  # not connected
  Part8 = I2C level shifter bidirectional  # not connected
  HC-SR04_Sensor_2 = HC-SR04 Ultrasonic Distance Sensor
  M8 = RPlidar A2M8 [package=THT]  # not connected
  DC_Mot_Enc5 = DC Motor with two-phase hall-encoder [part_number=VT-E-G25A-06-177E]
  DC_Mot_Enc6 = DC Motor with two-phase hall-encoder [part_number=VT-E-G25A-06-177E]
  DC_Mot_Enc7 = DC Motor with two-phase hall-encoder [part_number=VT-E-G25A-06-177E]
  DC_Mot_Enc8 = DC Motor with two-phase hall-encoder [part_number=VT-E-G25A-06-177E]
  Part9 = Arduino Nano (Rev3.0)
  Mod1 = Raspberry Pi Pico W  # not connected
  JP1 = Header 5x2 [package=2x5-ra]
  JP2 = Header 5x2 [package=2x5-ra]  # not connected
  JP3 = Header 5x2 [package=2x5-ra]
  JP4 = Header 5x2 [package=2x5-ra]
  J1 = STARBOARD_GND [package=starboard_ground_small2]
  J2 = STARBOARD_GND [package=starboard_ground_small2]
  J3 = STARBOARD_GND [package=starboard_ground_small2]

nets:
  N1: Part1.D1/TX, Part6.HV2
  N2: Part1.D0/RX, Part6.HV1
  GND: Part1.GND, HC-SR04_Sensor_1.GND, M3.pin2, Part3.GND, Part6.GND
  VCC: Part1.5V, HC-SR04_Sensor_1.VCC, M3.pin3, Part3.VCC, Part6.HV
  N3: Part1.A5, M4.pin1
  N4: Part1.3V3, Part6.LV
  N5: U1.+, M2.Pin_1
  N6: U1.-, M2.Pin_2
  N7: U3.+, M5.Pin_1
  N8: U3.-, M5.Pin_2, A6.Pin_5, A6.Pin_11, A7.Pin_4, J2.MOUNT
  N9: M6.pin1, Part9.A1
  N10: M6.pin2, JP1.6
  N11: M6.pin3, M7.pin3, A7.Pin_5, Part9.5V
  GND_2: M7.pin2, Part7.GND, HC-SR04_Sensor_2.GND, DC_Mot_Enc5.pin2, DC_Mot_Enc7.pin2, Part9.GND, J1.MOUNT
  N12: A6.Pin_6, JP1.1
  N13: A6.Pin_7, JP4.1
  N14: A6.Pin_8, JP4.3
  VCC_2: Part7.VCC, HC-SR04_Sensor_2.VCC, Part9.3V3
  N15: A7.Pin_1, JP1.8
  N16: A7.Pin_2, JP1.10
  N17: DC_Mot_Enc5.pin3, JP4.4
  N18: DC_Mot_Enc5.pin4, JP4.2
  N19: DC_Mot_Enc6.pin2, DC_Mot_Enc8.pin2, J3.MOUNT
  N20: DC_Mot_Enc6.pin3, JP4.10
  N21: DC_Mot_Enc6.pin4, JP4.8
  N22: DC_Mot_Enc7.pin3, JP3.1
  N23: DC_Mot_Enc7.pin4, JP3.3
  N24: DC_Mot_Enc8.pin3, JP3.4
  N25: DC_Mot_Enc8.pin4, JP3.2

notes:
  REd=5V/6V power,
  Pink = Signal,
  Black = ground, Orange = 3.3V power
  green/yellow = I2C-ish signal pairs
  SR04 is 5V. Fish sensor is 5V
  motors - encoder can be 3.3-5V. Output will be according to input
  Vl53L5CX is 3.3V power and
  https://learn.sparkfun.com/tutorials/qwiic-tof-imager---vl53l5cx-hookup-guide
  LD2450 power is 5V,200mA. It's Serial port (UART?) TxRx is 3.3V, default baud 256k
  MPU6050 is 3.3 or 5V as per power supply
  ESP32-Pico pins GP39 and GND are interchanged in this model. But onreal piece they are as per datasheet
  Nano V3 is 5V device . Power will be from micro- USB at 5V from the Jetson
  Nano V3 is 5V device . Power will be from micro- USB at 5V from the Jetson
  SDA A4(23), SCL A5(24)

custom parts:
  RPlidar A2M8: .The RPLIDAR A2 is the next generation low cost 360 degree 2D laser scanner (LIDAR) solution developed by SLAMTEC. It can take up to 4000 samples of laser ranging per second with high rotation speed. And equipped with SLAMTEC patented OPTMAG technology, it breakouts the life limitation of traditional LIDAR system so as to work stably for a long time.
  Sparkfun sen18642: The SparkFun Qwiic ToF Imager is built around VL53L5CX from ST Electronics; a state of the art, Time-of-Flight (ToF), multizone ranging sensor.
  Hi-link HLK-LD2410C: LD2410C is a high-sensitivity 24GHz human presence status sensing module. bb reversed for on perfboard in breadboard.
  Raspberry Pi Pico W: Raspberry Pi Pico W. Based around the RP2040 microcontroller the Pico W is a low cost microcontroller device bringing Raspberry Pi quality, cost, and easy of use to the microcontroller space. The areas marked KEEPOUT in pcb silkscreen should not have traces running through them to avoid shorts on a soldered in module!
